# Fritzing sketch wiring (saved by Fritzing 0.9.5d)
stripboards: 1

parts:
  A1 = XIAO ESP32C3-smd
  Part1 = Adafruit TPS61023 [part_number="Adafruit #4654"]
  R2 = Resistor [tolerance=±5% resistance=220k package="2010 [SMD]"]
  R3 = Resistor [tolerance=±5% resistance=220k package="0603 [SMD]"]
  S1 = Round Pushbutton
  U1 = LIPO-1000mAh [package=lipo-1000]
  U2 = WS2812 RGB LED strip
  U3 = WS2812 RGB LED strip
  U4 = WS2812 RGB LED strip
  R4 = Resistor [tolerance=±5% resistance=10k package=THT]

nets:
  GND: A1.Pin_7, Part1.GND, R3.Pin_0, S1.leg0, U1.-, U2.GND, U3.GND, U4.GND, R4.Pin_0
  N1: A1.Pin_8, Part1.VIN, R2.Pin_0, U1.+
  N2: A1.Pin_9, R2.Pin_1
  N3: A1.Pin_10, S1.leg1
  N4: A1.Pin_16, Part1.EN, R4.Pin_1
  N5: A1.Pin_17, U2.DIN, U3.DIN, U4.DIN
  VCC: Part1.VDD, U2.VCC, U3.VCC, U4.VCC

custom parts:
  XIAO ESP32C3-smd: Seeed Studio XIAO ESP32C3 adopts new RISC-V architecture, supporting both Wi-Fi and BLE wireless connectivities.
  Adafruit TPS61023: This adorable little board will come in very handy whenever you need a good amount of 5V power. It's the size of a linear regulator, but it's actually a mini-booster! Input 2-5VDC on one side, and get 5V at up to 1A supply on the other. Perfect for use with battery-powered projects with 2 or 3 Alkaline, or a single Lithium battery. This booster uses a very small but thermally efficient chip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
  WS2812 RGB LED strip: WS2812 strip
